// Logisim project CPU.circ as structural Verilog: 30 circuits, main circuit main
module main (
  input  Line___Reset
);

  wire Clck, fourbitequals_1_outputvalue, fourbitequals_4_outputvalue, fourbitequals_5_outputvalue,
       fourbitequals_6_outputvalue, fourbitequals_7_outputvalue, fourbitequals_8_outputvalue,
       fourbitequals_9_outputvalue, fourbitequals_10_outputvalue, fourbitequals_11_outputvalue,
       fourbitequals_12_outputvalue, fourbitequals_13_outputvalue, fourbitequals_14_outputvalue,
       fourbitequals_15_outputvalue, fourbitequals_16_outputvalue, fourbitequals_17_outputvalue, or_1_out,
       or_2_out, or_3_out, or_4_out, or_5_out, or_6_out, or_7_out, or_9_out, or_10_out, or_11_out, RAMRE,
       RAMWE, RegWE;
  wire [3:0] Command, Nibble1, Nibble2, Nibble3, Nibble4, Nibble5, Nibble6, Nibble7, RegReadAddress1,
       RegReadAddress2, RegWriteAddress;
  wire [7:0] RAMAddress;
  wire [15:0] ALUOutput, BLUOutput, ConditionalJump, LineNumber, multiplexer_7_out, multiplexer_8_out,
       RAMInput, RamOutput, RegIn, RegOutput2, sixteenbitefficientalu_1_outputvalue,
       sixteenbithalfadder_1_outputvalue, sixteenbithalfadder_2_outputvalue;

  ROM #(.addrWidth(16), .dataWidth(32)) Code (
    .addr(LineNumber), .data({Command, Nibble1, Nibble2, Nibble3, Nibble4, Nibble5, Nibble6, Nibble7}));
  Hex_Digit_Display hex_digit_display_1 (.value(RAMInput[3:0]));  // open: dp
  Multiplexer #(.width(16), .enable("false")) multiplexer_1 (
    .in0(sixteenbithalfadder_1_outputvalue), .in1({Nibble1, Nibble2, Nibble3, Nibble4}),
    .out(ConditionalJump), .sel(sixteenbitefficientalu_1_outputvalue[0]));
  Hex_Digit_Display hex_digit_display_2 (.value(RAMInput[11:8]));  // open: dp
  Hex_Digit_Display hex_digit_display_3 (.value(RAMInput[7:4]));  // open: dp
  FourBitEquals fourbitequals_1 (.InputOne(Command), .InputTwo(4'b0111), .OutputValue(fourbitequals_1_outputvalue));
  Hex_Digit_Display hex_digit_display_4 (.value(RAMInput[15:12]));  // open: dp
  Registers ImportantNumbers (
    .InputValue(RegIn), .Clock(Clck), .WriteEnable(RegWE), .ReadAddress1(RegReadAddress1),
    .WriteAddress(RegWriteAddress), .ReadAddress2(RegReadAddress2), .Reset(fourbitequals_1_outputvalue),
    .OutputValue1(RAMInput), .OutputValue2(RegOutput2));
  SixteenBitEfficientALU sixteenbitefficientalu_1 (
    .Num2(RegOutput2), .Num1(RAMInput), .WhichOP(Nibble7[1:0]),
    .OutputValue(sixteenbitefficientalu_1_outputvalue));  // open: ExpectedSign
  FourBitEquals fourbitequals_2 (.InputOne(Command), .InputTwo(4'b1100), .OutputValue(RAMRE));
  SixteenBitHalfAdder sixteenbithalfadder_1 (
    .InputCarry(1'b1), .Num1(LineNumber), .OutputValue(sixteenbithalfadder_1_outputvalue));  // open: Num2
  RAM #(.dataWidth(16), .databus("bibus")) Numbers (
    .addr(RAMAddress), .we(RAMWE), .oe(RAMRE), .clk(Clck), .din(RAMInput), .dout(RamOutput));
  Clock clock_1 (.out(Clck));
  SixteenBitEfficientALU sixteenbitefficientalu_2 (
    .Num2(RegOutput2), .Num1(RAMInput), .WhichOP(Command[1:0]), .OutputValue(ALUOutput));  // open: ExpectedSign
  Multiplexer #(.select(4), .width(4), .enable("false")) multiplexer_2 (
    .in0(Nibble3), .in1(Nibble3), .in2(Nibble3), .in3(Nibble3), .in5(Nibble1), .in6(Nibble2), .in8(Nibble3),
    .in9(Nibble3), .in10(Nibble3), .in11(Nibble2), .in12(Nibble3), .in14(Nibble2), .out(RegWriteAddress),
    .sel(Command));  // open: in4, in7, in13, in15
  Hex_Digit_Display hex_digit_display_5 (.value(RegOutput2[7:4]));  // open: dp
  Hex_Digit_Display hex_digit_display_6 (.value(RegOutput2[3:0]));  // open: dp
  Hex_Digit_Display hex_digit_display_7 (.value(RegOutput2[15:12]));  // open: dp
  Hex_Digit_Display hex_digit_display_8 (.value(RegOutput2[11:8]));  // open: dp
  FourBitEquals fourbitequals_3 (.InputOne(Command), .InputTwo(4'b1101), .OutputValue(RAMWE));
  Multiplexer #(.select(4), .width(8), .enable("false")) multiplexer_3 (
    .in12({Nibble1, Nibble2}), .in13({Nibble1, Nibble2}), .out(RAMAddress), .sel(Command));  // open: in0, in1, in2, in3, in4, in5, in6, in7, in8, in9, in10, in11, in14, in15
  Multiplexer #(.select(4), .width(16), .enable("false")) multiplexer_4 (
    .in0(ALUOutput), .in1(ALUOutput), .in2(ALUOutput), .in3(ALUOutput),
    .in5({Nibble2, Nibble3, Nibble4, Nibble5}), .in6(RAMInput), .in8(BLUOutput), .in9(BLUOutput),
    .in10(BLUOutput), .in11(BLUOutput), .in12(RamOutput), .in14(BLUOutput), .out(RegIn), .sel(Command));  // open: in4, in7, in13, in15
  BLU blu_1 (.Num1(RAMInput), .Num2(RegOutput2), .Choice(Command), .OutputValue(BLUOutput));
  FourBitEquals fourbitequals_4 (.InputOne(Command), .InputTwo(4'b0000), .OutputValue(fourbitequals_4_outputvalue));
  FourBitEquals fourbitequals_5 (.InputOne(Command), .InputTwo(4'b0001), .OutputValue(fourbitequals_5_outputvalue));
  FourBitEquals fourbitequals_6 (.InputOne(Command), .InputTwo(4'b0010), .OutputValue(fourbitequals_6_outputvalue));
  FourBitEquals fourbitequals_7 (.InputOne(Command), .InputTwo(4'b0011), .OutputValue(fourbitequals_7_outputvalue));
  FourBitEquals fourbitequals_8 (.InputOne(Command), .InputTwo(4'b0101), .OutputValue(fourbitequals_8_outputvalue));
  FourBitEquals fourbitequals_9 (.InputOne(Command), .InputTwo(4'b0110), .OutputValue(fourbitequals_9_outputvalue));
  FourBitEquals fourbitequals_10 (.InputOne(Command), .InputTwo(4'b1000), .OutputValue(fourbitequals_10_outputvalue));
  FourBitEquals fourbitequals_11 (.InputOne(Command), .InputTwo(4'b1001), .OutputValue(fourbitequals_11_outputvalue));
  Multiplexer #(.select(4), .width(4), .enable("false")) multiplexer_5 (
    .in0(Nibble1), .in1(Nibble1), .in2(Nibble1), .in3(Nibble1), .in6(Nibble1), .in8(Nibble1), .in9(Nibble1),
    .in10(Nibble1), .in11(Nibble1), .in13(Nibble3), .in14(Nibble1), .in15(Nibble5), .out(RegReadAddress1),
    .sel(Command));  // open: in4, in5, in7, in12
  or or_1 (or_1_out, fourbitequals_4_outputvalue, fourbitequals_5_outputvalue);
  or or_2 (or_2_out, fourbitequals_10_outputvalue, fourbitequals_11_outputvalue);
  Register #(.width(16), .trigger("falling")) register_1 (
    .D(multiplexer_7_out), .en(1'b1), .clk(Clck), .Q(LineNumber), .clr(Line___Reset));
  or or_3 (or_3_out, fourbitequals_6_outputvalue, fourbitequals_7_outputvalue);
  or or_4 (or_4_out, fourbitequals_8_outputvalue, fourbitequals_9_outputvalue);
  or or_5 (or_5_out, or_1_out, or_3_out);
  or or_6 (or_6_out, or_4_out, or_2_out);
  Multiplexer #(.select(4), .width(4), .enable("false")) multiplexer_6 (
    .in0(Nibble2), .in1(Nibble2), .in2(Nibble2), .in3(Nibble2), .in8(Nibble2), .in9(Nibble2), .in10(Nibble2),
    .in15(Nibble6), .out(RegReadAddress2), .sel(Command));  // open: in4, in5, in6, in7, in11, in12, in13, in14
  or or_7 (or_7_out, or_5_out, or_6_out);
  or or_8 (RegWE, or_7_out, or_10_out);
  FourBitEquals fourbitequals_12 (.InputOne(Command), .InputTwo(4'b1010), .OutputValue(fourbitequals_12_outputvalue));
  or or_9 (or_9_out, fourbitequals_12_outputvalue, fourbitequals_13_outputvalue);
  FourBitEquals fourbitequals_13 (.InputOne(Command), .InputTwo(4'b1011), .OutputValue(fourbitequals_13_outputvalue));
  FourBitEquals fourbitequals_14 (.InputOne(Command), .InputTwo(4'b1100), .OutputValue(fourbitequals_14_outputvalue));
  FourBitEquals fourbitequals_15 (.InputOne(Command), .InputTwo(4'b1110), .OutputValue(fourbitequals_15_outputvalue));
  SixteenBitHalfAdder sixteenbithalfadder_2 (
    .InputCarry(1'b1), .Num1(LineNumber), .OutputValue(sixteenbithalfadder_2_outputvalue));  // open: Num2
  Multiplexer #(.width(16), .enable("false")) multiplexer_7 (
    .in0(multiplexer_8_out), .in1(ConditionalJump), .out(multiplexer_7_out),
    .sel(fourbitequals_16_outputvalue));
  FourBitEquals fourbitequals_16 (.InputOne(Command), .InputTwo(4'b1111), .OutputValue(fourbitequals_16_outputvalue));
  or or_10 (or_10_out, or_9_out, or_11_out);
  or or_11 (or_11_out, fourbitequals_14_outputvalue, fourbitequals_15_outputvalue);
  Multiplexer #(.width(16), .enable("false")) multiplexer_8 (
    .in0(sixteenbithalfadder_2_outputvalue), .in1({Nibble1, Nibble2, Nibble3, Nibble4}),
    .out(multiplexer_8_out), .sel(fourbitequals_17_outputvalue));
  FourBitEquals fourbitequals_17 (.InputOne(Command), .InputTwo(4'b0100), .OutputValue(fourbitequals_17_outputvalue));

  // Other names for the same wires on the sheet: RegOutput1[15:0] = RAMInput

  // Notes on the sheet:
  //   contents of Code (hex, n*v repeats v):
  //   50002a00 51004500 5200db00 230000 13140000 5500c000 34560000 57000000 26780000 d0180000 59000100
  //   89a0000 f0000a93 c01f0000 8f8f0000 9f8f0000 58000000 a8ff0000 1fff0000 bff00000 eff00000 6fe00000
  //   d00e0000 40017000
  //   This determines what the line number will be when conditional jump is called.
  //   Reading from ram is enabled if it is the register load command
  //   All ram inputs are from registers
  //   If it is the ram set command.
  //   Decide register write address depending on command.
  //   Decides register input depending on command
  //   Unit for all logic operations.
  //   Decides the RAM address depending on the command.
  //   Checks if the current command is a command that writes to the register bank.
  //   Line Number Control Center: It increments the line number.
  //   Decide register read address 1 depending on command 
  //   Decide register read address 2 depending on command 
  //   Decide input depending if the conditional jump command is being used
  //   Decide input depending if the jump command is being used
endmodule

module Registers (
  input  [15:0] InputValue,
  input  Clock,
  input  WriteEnable,
  input  [3:0] ReadAddress1,
  input  [3:0] WriteAddress,
  input  [3:0] ReadAddress2,
  input  Reset,
  output [15:0] OutputValue1,
  output [15:0] OutputValue2
);

  wire Register0, Register1, Register2, Register3, Register4, Register5, Register6, Register7, Register8,
       Register9, Register10, Register11, Register12, Register13, Register14, Register15;
  wire [15:0] register_1_q, register_2_q, register_3_q, register_4_q, register_5_q, register_6_q,
       register_7_q, register_8_q, register_9_q, register_10_q, register_11_q, register_12_q, register_13_q,
       register_14_q, register_15_q, register_16_q;

  Register #(.width(16)) register_1 (.D(InputValue), .en(Register0), .clk(Clock), .Q(register_1_q), .clr(Reset));
  Register #(.width(16)) register_2 (.D(InputValue), .en(Register1), .clk(Clock), .Q(register_2_q), .clr(Reset));
  Register #(.width(16)) register_3 (.D(InputValue), .en(Register2), .clk(Clock), .Q(register_3_q), .clr(Reset));
  Register #(.width(16)) register_4 (.D(InputValue), .en(Register3), .clk(Clock), .Q(register_4_q), .clr(Reset));
  Register #(.width(16)) register_5 (.D(InputValue), .en(Register4), .clk(Clock), .Q(register_5_q), .clr(Reset));
  Register #(.width(16)) register_6 (.D(InputValue), .en(Register5), .clk(Clock), .Q(register_6_q), .clr(Reset));
  Register #(.width(16)) register_7 (.D(InputValue), .en(Register6), .clk(Clock), .Q(register_7_q), .clr(Reset));
  Register #(.width(16)) register_8 (.D(InputValue), .en(Register7), .clk(Clock), .Q(register_8_q), .clr(Reset));
  Register #(.width(16)) register_9 (.D(InputValue), .en(Register8), .clk(Clock), .Q(register_9_q), .clr(Reset));
  Register #(.width(16)) register_10 (.D(InputValue), .en(Register9), .clk(Clock), .Q(register_10_q), .clr(Reset));
  Register #(.width(16)) register_11 (.D(InputValue), .en(Register10), .clk(Clock), .Q(register_11_q), .clr(Reset));
  Register #(.width(16)) register_12 (.D(InputValue), .en(Register11), .clk(Clock), .Q(register_12_q), .clr(Reset));
  Register #(.width(16)) register_13 (.D(InputValue), .en(Register12), .clk(Clock), .Q(register_13_q), .clr(Reset));
  Register #(.width(16)) register_14 (.D(InputValue), .en(Register13), .clk(Clock), .Q(register_14_q), .clr(Reset));
  Register #(.width(16)) register_15 (.D(InputValue), .en(Register14), .clk(Clock), .Q(register_15_q), .clr(Reset));
  Register #(.width(16)) register_16 (.D(InputValue), .en(Register15), .clk(Clock), .Q(register_16_q), .clr(Reset));
  Multiplexer #(.select(4), .width(16), .enable("false")) multiplexer_1 (
    .in0(register_1_q), .in1(register_2_q), .in2(register_3_q), .in3(register_4_q), .in4(register_5_q),
    .in5(register_6_q), .in6(register_7_q), .in7(register_8_q), .in8(register_9_q), .in9(register_10_q),
    .in10(register_11_q), .in11(register_12_q), .in12(register_13_q), .in13(register_14_q),
    .in14(register_15_q), .in15(register_16_q), .out(OutputValue2), .sel(ReadAddress2));
  Multiplexer #(.select(4), .width(16), .enable("false")) multiplexer_2 (
    .in0(register_1_q), .in1(register_2_q), .in2(register_3_q), .in3(register_4_q), .in4(register_5_q),
    .in5(register_6_q), .in6(register_7_q), .in7(register_8_q), .in8(register_9_q), .in9(register_10_q),
    .in10(register_11_q), .in11(register_12_q), .in12(register_13_q), .in13(register_14_q),
    .in14(register_15_q), .in15(register_16_q), .out(OutputValue1), .sel(ReadAddress1));
  Demultiplexer #(.select(4), .enable("false")) demultiplexer_1 (
    .out0(Register0), .out1(Register1), .out2(Register2), .out3(Register3), .out4(Register4),
    .out5(Register5), .out6(Register6), .out7(Register7), .out8(Register8), .out9(Register9),
    .out10(Register10), .out11(Register11), .out12(Register12), .out13(Register13), .out14(Register14),
    .out15(Register15), .in(WriteEnable), .sel(WriteAddress));
endmodule

module OverflowChecker (
  input  [15:0] Num2,
  input  [15:0] Num1,
  input  [15:0] InputValue,
  output ExpectedSign
);

  wire multiplexer_1_out, not_1_out, xor_1_out, xor_2_out;

  xor xor_1 (xor_1_out, Num2[15], Num1[15]);
  not not_1 (not_1_out, xor_1_out);
  xor xor_2 (xor_2_out, Num2[15], InputValue[15]);
  Multiplexer #(.enable("false")) multiplexer_1 (.in0(1'b0), .in1(xor_2_out), .out(multiplexer_1_out), .sel(not_1_out));
  Multiplexer #(.enable("false")) multiplexer_2 (
    .in0(InputValue[15]), .in1(Num2[15]), .out(ExpectedSign), .sel(multiplexer_1_out));
endmodule

module MultiFLEXer (
  input  [15:0] Num1,
  input  [15:0] Num2,
  input  Choice,
  output [15:0] OutputValue
);

  wire [15:0] not_1_out, not_2_out, not_3_out, not_4_out, not_5_out, or_1_out, or_2_out;

  assign not_1_out = ~Num1;  // NOT_Gate not_1, 16 bits wide
  assign not_2_out = ~Num2;  // NOT_Gate not_2, 16 bits wide
  assign not_3_out = ~{16{Choice}};  // NOT_Gate not_3, 16 bits wide
  assign or_1_out = not_1_out | {16{Choice}};  // OR_Gate or_1, 16 bits wide
  assign not_4_out = ~or_1_out;  // NOT_Gate not_4, 16 bits wide
  assign or_2_out = not_2_out | not_3_out;  // OR_Gate or_2, 16 bits wide
  assign not_5_out = ~or_2_out;  // NOT_Gate not_5, 16 bits wide
  assign OutputValue = not_4_out | not_5_out;  // OR_Gate or_3, 16 bits wide
endmodule

module SixteenBitEfficientALU (
  input  [15:0] Num2,
  input  [15:0] Num1,
  input  [1:0] WhichOP,
  output ExpectedSign,
  output [15:0] OutputValue
);

  wire and_1_out, not_2_out, not_3_out, or_1_out;
  wire [0:0] and_2_out, sixteenbitequalsto_1_out_2;
  wire [15:0] multiflexer_1_outputvalue, multiplexer_1_out, multiplexer_2_out, not_1_out,
       sixteenbithalfadder_1_outputvalue, sixteenbitnegator_1_outputvalue;

  and and_1 (and_1_out, WhichOP[1], WhichOP[0]);
  or or_1 (or_1_out, WhichOP[0], WhichOP[1]);
  Multiplexer #(.width(16), .enable("false")) multiplexer_1 (
    .in0(Num2), .in1(not_1_out), .out(multiplexer_1_out), .sel(or_1_out));
  assign not_1_out = ~Num2;  // NOT_Gate not_1, 16 bits wide
  SixteenBitHalfAdder sixteenbithalfadder_1 (
    .InputCarry(or_1_out), .Num1(Num1), .Num2(multiplexer_1_out),
    .OutputValue(sixteenbithalfadder_1_outputvalue));
  Multiplexer #(.width(16), .enable("false")) multiplexer_2 (
    .in0(multiplexer_1_out), .in1(sixteenbitnegator_1_outputvalue), .out(multiplexer_2_out), .sel(or_1_out));
  SixteenBitNegator sixteenbitnegator_1 (.Num(multiplexer_1_out), .OutputValue(sixteenbitnegator_1_outputvalue));
  OverflowChecker overflowchecker_1 (
    .Num2(multiplexer_2_out), .Num1(Num1), .InputValue(sixteenbithalfadder_1_outputvalue),
    .ExpectedSign(ExpectedSign));
  SixteenBitEqualsTo sixteenbitequalsto_1 (.InputValue({Num1, Num2}), .out_2(sixteenbitequalsto_1_out_2[0]));
  not not_2 (not_2_out, ExpectedSign);
  not not_3 (not_3_out, sixteenbitequalsto_1_out_2[0]);
  and and_2 (and_2_out[0], not_3_out, not_2_out);
  MultiFLEXer multiflexer_1 (
    .Num1(sixteenbithalfadder_1_outputvalue), .Num2({{15{1'b0}}, and_2_out[0]}), .Choice(WhichOP[1]),
    .OutputValue(multiflexer_1_outputvalue));
  MultiFLEXer multiflexer_2 (
    .Num1(multiflexer_1_outputvalue), .Num2({{15{1'b0}}, sixteenbitequalsto_1_out_2[0]}), .Choice(and_1_out),
    .OutputValue(OutputValue));

  // Notes on the sheet:
  //   00: adding, 01: subtracting, 10: greater than, 11: equal to
  //   Adding And Subtracting
  //   EqualTo
  //   Greater Than
  //   If you did greater than or equal to, 1 is true and 0 is false.
endmodule

module EightBitEfficientALU (
  input  [7:0] Num2,
  input  [7:0] Num1,
  input  [1:0] Choice,
  output out_4,
  output [7:0] OutputValue
);

  wire and_1_out, not_2_out, not_3_out, or_1_out;
  wire [0:0] and_2_out, eightbitequalto_1_outputvalue;
  wire [7:0] eightbithalfadder_1_outputvalue, multiplexer_1_out, multiplexer_2_out, not_1_out;

  and and_1 (and_1_out, Choice[1], Choice[0]);
  or or_1 (or_1_out, Choice[0], Choice[1]);
  Multiplexer #(.width(8), .enable("false")) multiplexer_1 (
    .in0(Num2), .in1(not_1_out), .out(multiplexer_1_out), .sel(or_1_out));
  assign not_1_out = ~Num2;  // NOT_Gate not_1, 8 bits wide
  EightBitHalfAdder eightbithalfadder_1 (
    .InputCarry(or_1_out), .Num1(Num1), .Num2(multiplexer_1_out),
    .OutputValue(eightbithalfadder_1_outputvalue));
  EightBitEqualTo eightbitequalto_1 (.Num1(Num2), .Num2(Num1), .OutputValue(eightbitequalto_1_outputvalue[0]));
  EightBitOverflowChecker eightbitoverflowchecker_1 (
    .Num1(Num1), .Num2(multiplexer_1_out), .InputValue(eightbithalfadder_1_outputvalue), .ExpectedSign(out_4));
  not not_2 (not_2_out, out_4);
  not not_3 (not_3_out, eightbitequalto_1_outputvalue[0]);
  and and_2 (and_2_out[0], not_3_out, not_2_out);
  Multiplexer #(.width(8), .enable("false")) multiplexer_2 (
    .in0(eightbithalfadder_1_outputvalue), .in1({{7{1'b0}}, and_2_out[0]}), .out(multiplexer_2_out),
    .sel(Choice[1]));
  Multiplexer #(.width(8), .enable("false")) multiplexer_3 (
    .in0(multiplexer_2_out), .in1({{7{1'b0}}, eightbitequalto_1_outputvalue[0]}), .out(OutputValue),
    .sel(and_1_out));

  // Notes on the sheet:
  //   00: adding, 01: subtracting, 10: greater than, 11: equal to
  //   Adding And Subtracting
  //   EqualTo
  //   Greater Than
  //   If you did greater than or equal to, 1 is true and 0 is false.
endmodule

module OneBitAdder (
  input  Num1,
  input  Num2,
  input  InputCarry,
  output OutputValue,
  output OutputCarry
);

  wire and_1_out, and_2_out, and_3_out, or_1_out, xor_1_out;

  xor xor_1 (xor_1_out, Num1, Num2);
  xor xor_2 (OutputValue, xor_1_out, InputCarry);
  and and_1 (and_1_out, Num1, Num2);
  and and_2 (and_2_out, Num1, InputCarry);
  and and_3 (and_3_out, Num2, InputCarry);
  or or_1 (or_1_out, and_1_out, and_2_out);
  or or_2 (OutputCarry, or_1_out, and_3_out);
endmodule

module TwoBitAdder (
  input  [1:0] Num1,
  input  [1:0] Num2,
  input  InputCarry,
  output [1:0] OutputValue,
  output OutputCarry
);

  wire onebitadder_1_outputcarry;

  OneBitAdder onebitadder_1 (
    .Num1(Num1[0]), .Num2(Num2[0]), .InputCarry(InputCarry), .OutputValue(OutputValue[0]),
    .OutputCarry(onebitadder_1_outputcarry));
  OneBitAdder onebitadder_2 (
    .Num1(Num1[1]), .Num2(Num2[1]), .InputCarry(onebitadder_1_outputcarry), .OutputValue(OutputValue[1]),
    .OutputCarry(OutputCarry));
endmodule

module FourBitAdder (
  input  [3:0] Num1,
  input  InputCarry,
  input  [3:0] OutputValue,
  input  [3:0] Num2,
  output OutputCarry
);

  wire twobitadder_1_outputcarry;

  TwoBitAdder twobitadder_1 (
    .Num1(Num1[1:0]), .Num2(Num2[1:0]), .InputCarry(InputCarry), .OutputValue(OutputValue[1:0]),
    .OutputCarry(twobitadder_1_outputcarry));
  TwoBitAdder twobitadder_2 (
    .Num1(Num1[3:2]), .Num2(Num2[3:2]), .InputCarry(twobitadder_1_outputcarry),
    .OutputValue(OutputValue[3:2]), .OutputCarry(OutputCarry));
endmodule

module EightBitAdder (
  input  InputCarry,
  input  [7:0] Num1,
  input  [7:0] Num2,
  output [7:0] OutputValue,
  output OutputCarry
);

  wire and_1_out, and_2_out, and_3_out, and_4_out, and_5_out, and_6_out, and_7_out, and_8_out, and_9_out,
       and_10_out, and_11_out, and_12_out, and_13_out, and_14_out, and_15_out, and_16_out, and_17_out,
       and_18_out, and_19_out, and_20_out, and_21_out, and_22_out, and_23_out, and_24_out, or_1_out,
       or_2_out, or_3_out, or_4_out, or_5_out, or_6_out, or_7_out, or_8_out, or_9_out, or_10_out, or_11_out,
       or_12_out, or_13_out, or_14_out, or_15_out, xor_1_out, xor_2_out, xor_3_out, xor_4_out, xor_5_out,
       xor_6_out, xor_7_out, xor_8_out;

  xor xor_1 (xor_1_out, Num1[0], Num2[0]);
  xor xor_2 (xor_2_out, Num1[1], Num2[1]);
  xor xor_3 (xor_3_out, Num1[2], Num2[2]);
  xor xor_4 (xor_4_out, Num1[3], Num2[3]);
  xor xor_5 (xor_5_out, Num1[4], Num2[4]);
  xor xor_6 (xor_6_out, Num1[5], Num2[5]);
  xor xor_7 (xor_7_out, Num1[6], Num2[6]);
  xor xor_8 (xor_8_out, Num1[7], Num2[7]);
  xor xor_9 (OutputValue[0], xor_1_out, InputCarry);
  xor xor_10 (OutputValue[1], xor_2_out, or_9_out);
  xor xor_11 (OutputValue[2], xor_3_out, or_10_out);
  xor xor_12 (OutputValue[3], xor_4_out, or_11_out);
  xor xor_13 (OutputValue[4], xor_5_out, or_12_out);
  xor xor_14 (OutputValue[5], xor_6_out, or_13_out);
  xor xor_15 (OutputValue[6], xor_7_out, or_14_out);
  xor xor_16 (OutputValue[7], xor_8_out, or_15_out);
  and and_1 (and_1_out, Num1[0], Num2[0]);
  and and_2 (and_2_out, Num2[0], InputCarry);
  and and_3 (and_3_out, InputCarry, Num1[0]);
  and and_4 (and_4_out, Num1[1], Num2[1]);
  and and_5 (and_5_out, Num2[1], or_9_out);
  and and_6 (and_6_out, or_9_out, Num1[1]);
  and and_7 (and_7_out, Num1[2], Num2[2]);
  and and_8 (and_8_out, Num2[2], or_10_out);
  and and_9 (and_9_out, or_10_out, Num1[2]);
  and and_10 (and_10_out, Num1[3], Num2[3]);
  and and_11 (and_11_out, Num2[3], or_11_out);
  and and_12 (and_12_out, or_11_out, Num1[3]);
  and and_13 (and_13_out, Num1[4], Num2[4]);
  and and_14 (and_14_out, Num2[4], or_12_out);
  and and_15 (and_15_out, or_12_out, Num1[4]);
  and and_16 (and_16_out, Num1[5], Num2[5]);
  and and_17 (and_17_out, Num2[5], or_13_out);
  and and_18 (and_18_out, or_13_out, Num1[5]);
  and and_19 (and_19_out, Num1[6], Num2[6]);
  and and_20 (and_20_out, Num2[6], or_14_out);
  and and_21 (and_21_out, or_14_out, Num1[6]);
  and and_22 (and_22_out, Num1[7], Num2[7]);
  and and_23 (and_23_out, Num2[7], or_15_out);
  and and_24 (and_24_out, or_15_out, Num1[7]);
  or or_1 (or_1_out, and_7_out, and_8_out);
  or or_2 (or_2_out, and_10_out, and_11_out);
  or or_3 (or_3_out, and_19_out, and_20_out);
  or or_4 (or_4_out, and_22_out, and_23_out);
  or or_5 (or_5_out, and_1_out, and_2_out);
  or or_6 (or_6_out, and_4_out, and_5_out);
  or or_7 (or_7_out, and_13_out, and_14_out);
  or or_8 (or_8_out, and_16_out, and_17_out);
  or or_9 (or_9_out, or_5_out, and_3_out);
  or or_10 (or_10_out, or_6_out, and_6_out);
  or or_11 (or_11_out, or_1_out, and_9_out);
  or or_12 (or_12_out, or_2_out, and_12_out);
  or or_13 (or_13_out, or_7_out, and_15_out);
  or or_14 (or_14_out, or_8_out, and_18_out);
  or or_15 (or_15_out, or_3_out, and_21_out);
  or or_16 (OutputCarry, or_4_out, and_24_out);
endmodule

module SixteenBitAdder (
  input  InputCarry,
  input  [15:0] Num1,
  input  [15:0] Num2,
  output [15:0] OutputValue,
  output OutputCarry
);

  wire eightbitadder_1_outputcarry;

  EightBitAdder eightbitadder_1 (
    .InputCarry(InputCarry), .Num1(Num1[7:0]), .Num2(Num2[7:0]), .OutputValue(OutputValue[7:0]),
    .OutputCarry(eightbitadder_1_outputcarry));
  EightBitAdder eightbitadder_2 (
    .InputCarry(eightbitadder_1_outputcarry), .Num1(Num1[15:8]), .Num2(Num2[15:8]),
    .OutputValue(OutputValue[15:8]), .OutputCarry(OutputCarry));
endmodule

module SixteenBitAdderWithoutCarry (
  input  [15:0] Num1,
  input  [15:0] Num2,
  output [16:0] OutputValue
);

  SixteenBitAdder sixteenbitadder_1 (
    .InputCarry(1'b0), .Num1(Num1), .Num2(Num2), .OutputValue(OutputValue[15:0]),
    .OutputCarry(OutputValue[16]));

  // Notes on the sheet:
  //   Input Carry is a const because this special sixteenbit adder isn't used to make any higher level adders.
endmodule

module ThirtyTwoBitAdder (
  input  [31:0] Num1,
  input  [31:0] Num2,
  output [31:0] OutputValue,
  output OutputCarry
);

  wire sixteenbitadder_1_outputcarry;

  SixteenBitAdder sixteenbitadder_1 (
    .InputCarry(1'b0), .Num1(Num1[15:0]), .Num2(Num2[15:0]), .OutputValue(OutputValue[15:0]),
    .OutputCarry(sixteenbitadder_1_outputcarry));
  SixteenBitAdder sixteenbitadder_2 (
    .InputCarry(sixteenbitadder_1_outputcarry), .Num1(Num1[31:16]), .Num2(Num2[31:16]),
    .OutputValue(OutputValue[31:16]), .OutputCarry(OutputCarry));

  // Notes on the sheet:
  //   It is not possible to make a 64 bit adder in this program, so the input carry of this 32 bit adder is a constant.
endmodule

module TwoBitHalfAdder (
  input  [1:0] Num1,
  input  [1:0] Num2,
  input  InputCarry,
  output [1:0] OutputValue
);

  wire onebitadder_1_outputcarry, xor_1_out;

  xor xor_1 (xor_1_out, Num1[1], Num2[1]);
  OneBitAdder onebitadder_1 (
    .Num1(Num1[0]), .Num2(Num2[0]), .InputCarry(InputCarry), .OutputValue(OutputValue[0]),
    .OutputCarry(onebitadder_1_outputcarry));
  xor xor_2 (OutputValue[1], xor_1_out, onebitadder_1_outputcarry);
endmodule

module FourBitHalfAdder (
  input  InputCarry,
  input  [3:0] Num1,
  input  [3:0] Num2,
  output [3:0] OutputValue
);

  wire twobitadder_1_outputcarry;

  TwoBitAdder twobitadder_1 (
    .Num1(Num1[1:0]), .Num2(Num2[1:0]), .InputCarry(InputCarry), .OutputValue(OutputValue[1:0]),
    .OutputCarry(twobitadder_1_outputcarry));
  TwoBitHalfAdder twobithalfadder_1 (
    .Num1(Num1[3:2]), .Num2(Num2[3:2]), .InputCarry(twobitadder_1_outputcarry), .OutputValue(OutputValue[3:2]));
endmodule

module EightBitHalfAdder (
  input  InputCarry,
  input  [7:0] Num1,
  input  [7:0] Num2,
  output [7:0] OutputValue
);

  wire onebitadder_1_outputcarry, onebitadder_2_outputcarry, onebitadder_3_outputcarry,
       onebitadder_4_outputcarry;

  OneBitAdder onebitadder_1 (
    .Num1(Num1[0]), .Num2(Num2[0]), .InputCarry(InputCarry), .OutputValue(OutputValue[0]),
    .OutputCarry(onebitadder_1_outputcarry));
  OneBitAdder onebitadder_2 (
    .Num1(Num1[1]), .Num2(Num2[1]), .InputCarry(onebitadder_1_outputcarry), .OutputValue(OutputValue[1]),
    .OutputCarry(onebitadder_2_outputcarry));
  FourBitHalfAdder fourbithalfadder_1 (
    .InputCarry(onebitadder_4_outputcarry), .Num1(Num1[7:4]), .Num2(Num2[7:4]), .OutputValue(OutputValue[7:4]));
  OneBitAdder onebitadder_3 (
    .Num1(Num1[2]), .Num2(Num2[2]), .InputCarry(onebitadder_2_outputcarry), .OutputValue(OutputValue[2]),
    .OutputCarry(onebitadder_3_outputcarry));
  OneBitAdder onebitadder_4 (
    .Num1(Num1[3]), .Num2(Num2[3]), .InputCarry(onebitadder_3_outputcarry), .OutputValue(OutputValue[3]),
    .OutputCarry(onebitadder_4_outputcarry));
endmodule

module SixteenBitHalfAdder (
  input  InputCarry,
  input  [15:0] Num1,
  input  [15:0] Num2,
  output [15:0] OutputValue
);

  wire eightbitadder_1_outputcarry;

  EightBitAdder eightbitadder_1 (
    .InputCarry(InputCarry), .Num1(Num1[7:0]), .Num2(Num2[7:0]), .OutputValue(OutputValue[7:0]),
    .OutputCarry(eightbitadder_1_outputcarry));
  EightBitHalfAdder eightbithalfadder_1 (
    .InputCarry(eightbitadder_1_outputcarry), .Num1(Num1[15:8]), .Num2(Num2[15:8]),
    .OutputValue(OutputValue[15:8]));
endmodule

module TwoBitSubtactor (
  input  [1:0] Num1,
  input  [1:0] Num2,
  output [1:0] OutputValue
);

  wire [1:0] twobitnegator_1_outputvalue;

  TwoBitNegator twobitnegator_1 (.Num(Num2), .OutputValue(twobitnegator_1_outputvalue));
  TwoBitHalfAdder twobithalfadder_1 (
    .Num1(Num1), .Num2(twobitnegator_1_outputvalue), .InputCarry(1'b0), .OutputValue(OutputValue));
endmodule

module FourBitSubtractor (
  input  [3:0] Num1,
  input  [3:0] Num2,
  output [3:0] OutputValue
);

  wire [3:0] fourbitnegator_1_outputvalue;

  FourBitNegator fourbitnegator_1 (.Num(Num2), .OutputValue(fourbitnegator_1_outputvalue));
  FourBitHalfAdder fourbithalfadder_1 (
    .InputCarry(1'b0), .Num1(Num1), .Num2(fourbitnegator_1_outputvalue), .OutputValue(OutputValue));
endmodule

module EightBitSubtractor (
  input  [7:0] Num1,
  input  [7:0] Num2,
  output [7:0] OutputValue
);

  wire [7:0] eightbitnegator_1_outputvalue;

  EightBitNegator eightbitnegator_1 (.Num(Num2), .OutputValue(eightbitnegator_1_outputvalue));
  EightBitHalfAdder eightbithalfadder_1 (
    .InputCarry(1'b0), .Num1(Num1), .Num2(eightbitnegator_1_outputvalue), .OutputValue(OutputValue));
endmodule

module TwoBitNegator (
  input  [1:0] Num,
  output [1:0] OutputValue
);

  wire and_1_out;
  wire [1:0] not_1_out;

  assign not_1_out = ~Num;  // NOT_Gate not_1, 2 bits wide
  xor xor_1 (OutputValue[1], not_1_out[1], and_1_out);
  and and_1 (and_1_out, not_1_out[0], 1'b1);
  xor xor_2 (OutputValue[0], not_1_out[0], 1'b1);
endmodule

module FourBitNegator (
  input  [3:0] Num,
  output [3:0] OutputValue
);

  wire and_1_out, and_2_out, and_3_out;
  wire [3:0] not_1_out;

  assign not_1_out = ~Num;  // NOT_Gate not_1, 4 bits wide
  xor xor_1 (OutputValue[0], not_1_out[0], 1'b1);
  xor xor_2 (OutputValue[1], not_1_out[1], and_1_out);
  xor xor_3 (OutputValue[3], and_3_out, not_1_out[3]);
  and and_1 (and_1_out, 1'b1, not_1_out[0]);
  and and_2 (and_2_out, not_1_out[1], and_1_out);
  xor xor_4 (OutputValue[2], and_2_out, not_1_out[2]);
  and and_3 (and_3_out, and_2_out, not_1_out[2]);
endmodule

module EightBitNegator (
  input  [7:0] Num,
  output [7:0] OutputValue
);

  wire [7:0] not_1_out;

  assign not_1_out = ~Num;  // NOT_Gate not_1, 8 bits wide
  EightBitHalfAdder eightbithalfadder_1 (
    .InputCarry(1'b1), .Num1(not_1_out), .Num2({8{1'b0}}), .OutputValue(OutputValue));
endmodule

module SixteenBitNegator (
  input  [15:0] Num,
  output [15:0] OutputValue
);

  wire [15:0] not_1_out;

  assign not_1_out = ~Num;  // NOT_Gate not_1, 16 bits wide
  SixteenBitHalfAdder sixteenbithalfadder_1 (
    .InputCarry(1'b1), .Num1(not_1_out), .Num2({16{1'b0}}), .OutputValue(OutputValue));
endmodule

module EightBitGreaterThan (
  input  [7:0] Num1,
  input  [7:0] Num2,
  output OutputValue
);

  wire eightbitequalto_1_outputvalue, not_1_out;
  wire [7:0] eightbitsubtractor_1_outputvalue;

  EightBitSubtractor eightbitsubtractor_1 (.Num1(Num1), .Num2(Num2), .OutputValue(eightbitsubtractor_1_outputvalue));
  EightBitEqualTo eightbitequalto_1 (
    .Num1(eightbitsubtractor_1_outputvalue), .Num2({8{1'b0}}), .OutputValue(eightbitequalto_1_outputvalue));
  not not_1 (not_1_out, eightbitequalto_1_outputvalue);
  xor xor_1 (OutputValue, not_1_out, eightbitsubtractor_1_outputvalue[7]);

  // Notes on the sheet:
  //   If Num1 > Num2, output will be 1.
endmodule

module EightBitEqualTo (
  input  [7:0] Num1,
  input  [7:0] Num2,
  output OutputValue
);

  wire and_1_out, and_2_out, and_3_out, and_4_out, and_5_out, and_6_out, and_7_out, and_8_out, and_9_out,
       and_10_out, and_11_out, and_12_out, and_13_out, and_14_out;
  wire [7:0] eightbitsubtractor_1_outputvalue, not_1_out, not_2_out;

  EightBitSubtractor eightbitsubtractor_1 (.Num1(Num1), .Num2(Num2), .OutputValue(eightbitsubtractor_1_outputvalue));
  assign not_1_out = ~eightbitsubtractor_1_outputvalue;  // NOT_Gate not_1, 8 bits wide
  assign not_2_out = ~{8{1'b0}};  // NOT_Gate not_2, 8 bits wide
  and and_1 (and_1_out, not_1_out[0], not_2_out[0]);
  and and_2 (and_2_out, not_1_out[1], not_2_out[1]);
  and and_3 (and_3_out, not_1_out[2], not_2_out[2]);
  and and_4 (and_4_out, not_1_out[3], not_2_out[3]);
  and and_5 (and_5_out, not_1_out[4], not_2_out[4]);
  and and_6 (and_6_out, not_1_out[5], not_2_out[5]);
  and and_7 (and_7_out, not_1_out[6], not_2_out[6]);
  and and_8 (and_8_out, not_1_out[7], not_2_out[7]);
  and and_9 (and_9_out, and_1_out, and_2_out);
  and and_10 (and_10_out, and_3_out, and_4_out);
  and and_11 (and_11_out, and_5_out, and_6_out);
  and and_12 (and_12_out, and_7_out, and_8_out);
  and and_13 (and_13_out, and_9_out, and_10_out);
  and and_14 (and_14_out, and_11_out, and_12_out);
  and and_15 (OutputValue, and_13_out, and_14_out);

  // Notes on the sheet:
  //   If one, they are equal.
endmodule

module SixteenBitEqualsTo (
  input  [31:0] InputValue,
  output out_2
);

  wire or_4_out;
  wire [1:0] or_3_out;
  wire [3:0] or_2_out;
  wire [7:0] or_1_out;
  wire [15:0] xor_1_out;

  assign xor_1_out = InputValue[15:0] ^ InputValue[31:16];  // XOR_Gate xor_1, 16 bits wide
  assign or_1_out = xor_1_out[7:0] | xor_1_out[15:8];  // OR_Gate or_1, 8 bits wide
  assign or_2_out = or_1_out[3:0] | or_1_out[7:4];  // OR_Gate or_2, 4 bits wide
  assign or_3_out = or_2_out[1:0] | or_2_out[3:2];  // OR_Gate or_3, 2 bits wide
  or or_4 (or_4_out, or_3_out[1], or_3_out[0]);
  not not_1 (out_2, or_4_out);
endmodule

module EightBitOverflowChecker (
  input  [7:0] Num1,
  input  [7:0] Num2,
  input  [7:0] InputValue,
  output ExpectedSign
);

  wire multiplexer_1_out, not_1_out, xor_1_out, xor_2_out;

  xor xor_1 (xor_1_out, Num1[7], Num2[7]);
  not not_1 (not_1_out, xor_1_out);
  xor xor_2 (xor_2_out, Num1[7], InputValue[7]);
  Multiplexer #(.enable("false")) multiplexer_1 (.in0(1'b0), .in1(xor_2_out), .out(multiplexer_1_out), .sel(not_1_out));
  Multiplexer #(.enable("false")) multiplexer_2 (
    .in0(InputValue[7]), .in1(Num1[7]), .out(ExpectedSign), .sel(multiplexer_1_out));
endmodule

module BLU (
  input  [15:0] Num1,
  input  [15:0] Num2,
  input  [3:0] Choice,
  output [15:0] OutputValue
);

  wire [15:0] and_1_out, not_1_out, or_1_out, sixteenbitnegator_1_outputvalue, xor_1_out;

  assign and_1_out = Num1 & Num2;  // AND_Gate and_1, 16 bits wide
  assign or_1_out = Num1 | Num2;  // OR_Gate or_1, 16 bits wide
  assign xor_1_out = Num1 ^ Num2;  // XOR_Gate xor_1, 16 bits wide
  assign not_1_out = ~Num1;  // NOT_Gate not_1, 16 bits wide
  SixteenBitNegator sixteenbitnegator_1 (.Num(Num1), .OutputValue(sixteenbitnegator_1_outputvalue));
  Multiplexer #(.select(4), .width(16), .enable("false")) multiplexer_1 (
    .in8(and_1_out), .in9(or_1_out), .in10(xor_1_out), .in11(not_1_out),
    .in14(sixteenbitnegator_1_outputvalue), .out(OutputValue), .sel(Choice));  // open: in0, in1, in2, in3, in4, in5, in6, in7, in12, in13, in15
endmodule

module FourBitEquals (
  input  [3:0] InputOne,
  input  [3:0] InputTwo,
  output OutputValue
);

  wire or_2_out;
  wire [1:0] or_1_out;
  wire [3:0] xor_1_out;

  assign xor_1_out = InputOne ^ InputTwo;  // XOR_Gate xor_1, 4 bits wide
  assign or_1_out = xor_1_out[1:0] | xor_1_out[3:2];  // OR_Gate or_1, 2 bits wide
  or or_2 (or_2_out, or_1_out[0], or_1_out[1]);
  not not_1 (OutputValue, or_2_out);
endmodule
